# Fritzing sketch openAutoWater (saved by Fritzing 0.7.10b)

parts:
  Part1 = Moisture Sensor
  Arduino_Mini_Pro1 = Arduino Mini Pro
  K1 = Relay [part_number=FRS1B-S package=THT]

nets:
  N1: Part1.no_name_yet#connector8pin-8, Arduino_Mini_Pro1.GND, K1.COIL1
  N2: Part1.no_name_yet#connector9pin-2, Arduino_Mini_Pro1.D2
  N3: Part1.no_name_yet#connector9pin-2-6, Arduino_Mini_Pro1.A0
  N4: Arduino_Mini_Pro1.D3, K1.COIL2
